// Logisim project seven_segment_display.circ as structural Verilog: 1 circuit, main circuit main
module main (
  input  b0,
  input  b1,
  input  b2,
  input  b3
);

  wire and_1_out, and_2_out, not_1_out, not_3_out, or_1_out;

  not not_1 (not_1_out, b0);
  // NOT_Gate not_2 has open pins: in=b1, out=open
  not not_3 (not_3_out, b2);
  and and_1 (and_1_out, b0, b2);
  and and_2 (and_2_out, not_1_out, not_3_out);
  or or_1 (or_1_out, and_1_out, and_2_out, b1, b3);
  _7_Segment_Display u_7_segment_display_1 (.a(or_1_out));  // open: g, f, b, e, d, c, dp
endmodule
